// Logisim project risc5.circ as structural Verilog: 13 circuits, main circuit Projet_Processeur
module Projet_Processeur (
  input  [6:0] fonction_7bit,
  input  [4:0] registre_source_2,
  input  [4:0] registre_source_1,
  input  [2:0] fonction_3bit,
  input  [4:0] registre_destination,
  input  [6:0] code_operation,
  input  [11:0] \immédiate__11_0 ,
  input  [4:0] registre_source_1_2,
  input  in_9,
  input  [2:0] fonction_3bit_2,
  input  [4:0] registre_destination_2,
  input  [6:0] code_operation_2
);

  wire clk, clock_1_out;
  wire [3:0] cpu_1_flags;
  wire [31:0] fetch_addr, instruction, r0, r1, r2, r3, r4, r5, r6, r7, r8, r9, r10, r11, r12, r13, r14, r15,
       r16, r17, r18, r19, r20, r21, r22, r23, r24, r25, r26, r27, r28, r29, r30, r31;

  // Probe on r0
  // Probe on r8
  // Probe on r16
  // Probe on r24
  assign clk = in_9 ? clock_1_out : 1'bz;  // Controlled_Buffer controlled_buffer_1
  Clock clock_1 (.out(clock_1_out));
  // Probe on r1
  // Probe on r9
  // Probe on r17
  // Probe on r25
  // Probe on r2
  // Probe on r10
  // Probe on r18
  // Probe on r26
  // Probe on fetch_addr
  // Probe on fetch_addr
  // Probe on fetch_addr
  // Probe on r3
  // Probe on r11
  // Probe on r19
  // Probe on r27
  // Probe on r4
  // Probe on r12
  // Probe on r20
  // Probe on r28
  CPU cpu_1 (
    .instruction(instruction), .fetch_addr(fetch_addr), .out_3(r0), .out_9(r4), .out_13(r8), .out_17(r12),
    .out_21(r16), .out_25(r20), .out_29(r24), .out_33(r28), .out_4(r1), .out_10(r5), .out_14(r9),
    .out_18(r13), .out_22(r17), .out_26(r21), .out_30(r25), .out_34(r29), .out_5(r2), .out_11(r6),
    .out_15(r10), .out_19(r14), .out_23(r18), .out_27(r22), .out_31(r26), .out_35(r30), .out_6(r3),
    .out_12(r7), .out_16(r11), .out_20(r15), .out_24(r19), .out_28(r23), .out_32(r27), .out_36(r31),
    .in_1(clk), .FLAGS(cpu_1_flags));
  // Probe on r5
  // Probe on r13
  // Probe on r21
  // Probe on r29
  ROM #(.addrWidth(24), .dataWidth(32)) rom_1 (.addr(fetch_addr[23:0]), .data(instruction));  // open: sel
  // Probe on instruction
  // Probe on instruction
  // Probe on r6
  // Probe on r14
  // Probe on r22
  // Probe on r30
  // Probe on cpu_1_flags
  // Probe on r7
  // Probe on r15
  // Probe on r23
  // Probe on r31
  // Probe on {fonction_7bit, registre_source_2, registre_source_1, fonction_3bit, registre_destination, code_operation}
  // Probe on {\immédiate__11_0 , registre_source_1_2, fonction_3bit_2, registre_destination_2, code_operation_2}

  // Notes on the sheet:
  //   contents of rom_1 (hex, n*v repeats v):
  //   1f00093 108133 208193 310213
endmodule

module CPU (
  input  in_1,
  input  [31:0] instruction,
  output [31:0] out_3,
  output [31:0] out_4,
  output [31:0] out_5,
  output [31:0] out_6,
  output [31:0] fetch_addr,
  output [3:0] FLAGS,
  output [31:0] out_9,
  output [31:0] out_10,
  output [31:0] out_11,
  output [31:0] out_12,
  output [31:0] out_13,
  output [31:0] out_14,
  output [31:0] out_15,
  output [31:0] out_16,
  output [31:0] out_17,
  output [31:0] out_18,
  output [31:0] out_19,
  output [31:0] out_20,
  output [31:0] out_21,
  output [31:0] out_22,
  output [31:0] out_23,
  output [31:0] out_24,
  output [31:0] out_25,
  output [31:0] out_26,
  output [31:0] out_27,
  output [31:0] out_28,
  output [31:0] out_29,
  output [31:0] out_30,
  output [31:0] out_31,
  output [31:0] out_32,
  output [31:0] out_33,
  output [31:0] out_34,
  output [31:0] out_35,
  output [31:0] out_36
);

  wire add, addi, \and , andi, B_imm_11, B_sel, B_Type, beq, blt, bltu, div, I_Type, I_Type_imm, I_Type_Jalr,
       I_Type_jalr_t, I_Type_Load, imm_12, imm_20, J_imm_11, J_Type, jal, jalr, lb, lh, lui, lw, mul, mulh,
       \or , ori, R_Type, rem, reset, S_Type, sll, slli, slt, slti, srl, srli, sub, sw, swge, U_Type,
       writeEn, \xor , xori;
  wire [2:0] funct3;
  wire [3:0] imm_4_1, UAL_select;
  wire [4:0] imm_4_0, rd, rs1, rs2;
  wire [5:0] imm_10_5;
  wire [6:0] funct7, imm_11_5, opcode;
  wire [7:0] imm_19_12;
  wire [9:0] imm_10_1;
  wire [11:0] imm_11_0;
  wire [19:0] imm_31_12;
  wire [31:0] A, B, imm, imm_B_extend, imm_I_extend, imm_J_extend, imm_S_extend, imm_U_extend,
       multiplexer_1_out, PC, PC_4, res_alu;

  // Probe on funct3
  // Probe on funct3
  // Probe on res_alu
  LED led_1 (.in(R_Type));
  LED led_2 (.in(add));
  LED led_3 (.in(mul));
  LED led_4 (.in(sub));
  LED led_5 (.in(sll));
  LED led_6 (.in(mulh));
  LED led_7 (.in(slt));
  LED led_8 (.in(\xor ));
  LED led_9 (.in(div));
  LED led_10 (.in(srl));
  LED led_11 (.in(\or ));
  LED led_12 (.in(rem));
  LED led_13 (.in(\and ));
  // Probe on instruction
  \Décodeur_Instruction  \décodeur_instruction_1  (
    .fonction_7bit(funct7), .registre_source_2(rs2), .registre_source_1(rs1), .\immédiate__12 (imm_12),
    .\immédiate__20 (imm_20), .fonction_3bit(funct3), .\immédiate__10_5 (imm_10_5),
    .registre_destination(rd), .\immédiate__11_5 (imm_11_5), .\immédiate__4_1 (imm_4_1),
    .\immédiate__10_1 (imm_10_1), .\immédiate__31_12 (imm_31_12), .code_operation(opcode),
    .\immédiate__11_0 (imm_11_0), .\immédiate__4_0 (imm_4_0), .\B_immédiate__11 (B_imm_11),
    .\J_immédiate__11 (J_imm_11), .\immédiate__19_12 (imm_19_12), .Instruction(instruction));
  // Probe on opcode
  Filtre_Type filtre_type_1 (
    .R_Type(R_Type), .I_Type_Charge(I_Type_Load), .I_Type_Immediat(I_Type_imm), .I_Type_Jalr(I_Type_Jalr),
    .S_Type(S_Type), .B_Type(B_Type), .U_Type(U_Type), .J_Type(J_Type), .code_operation(opcode));
  LED led_14 (.in(R_Type));
  // Probe on funct7
  \Filtre_Opération_Type_R  \filtre_opération_type_r_1  (
    .add(add), .\xor (\xor ), .mul(mul), .div(div), .sub(sub), .srl(srl), .sll(sll), .\or (\or ),
    .mulh(mulh), .rem(rem), .slt(slt), .\and (\and ), .Fonction_3bit(funct3), .Fonction_7bit(funct7),
    .R_Type(R_Type));
  LED led_15 (.in(B_Type));
  LED led_16 (.in(S_Type));
  LED led_17 (.in(J_Type));
  LED led_18 (.in(U_Type));
  \Filtre_Opération_Type_S_B_U_J  \filtre_opération_type_s_b_u_j_1  (
    .U_Type(U_Type), .J_Type(J_Type), .sw(sw), .swge(swge), .beq(beq), .blt(blt), .bltu(bltu), .lui(lui),
    .jal(jal), .Fonction_3bit(funct3), .S_Type(S_Type), .B_Type(B_Type));
  // Probe on rd
  LED led_19 (.in(I_Type_Load));
  LED led_20 (.in(lb));
  LED led_21 (.in(lh));
  LED led_22 (.in(lw));
  LED led_23 (.in(I_Type_imm));
  LED led_24 (.in(addi));
  LED led_25 (.in(slli));
  LED led_26 (.in(slti));
  LED led_27 (.in(xori));
  LED led_28 (.in(srli));
  LED led_29 (.in(ori));
  LED led_30 (.in(andi));
  // Probe on rs1
  // Probe on rs2
  LED led_31 (.in(S_Type));
  LED led_32 (.in(sw));
  LED led_33 (.in(swge));
  LED led_34 (.in(B_Type));
  LED led_35 (.in(beq));
  LED led_36 (.in(blt));
  LED led_37 (.in(bltu));
  LED led_38 (.in(U_Type));
  LED led_39 (.in(lui));
  Compteur_De_Programme compteur_de_programme_1 (.PC_4(PC_4), .fetch_addr(fetch_addr), .PC(PC));
  LED led_40 (.in(J_Type));
  LED led_41 (.in(jal));
  // Probe on funct3
  // Probe on funct7
  LED led_42 (.in(I_Type_Jalr));
  Banc_De_Registre banc_de_registre_1 (
    .\écriture (writeEn), .horloge(in_1), .reset(reset), .in_7(res_alu), .out_9(B), .out_8(A), .adresse(rs1),
    .adresse_2(rs2), .adresse_3(rd), .out_10(out_3), .out_11(out_4), .out_12(out_5), .out_13(out_6),
    .out_14(out_9), .out_15(out_10), .out_16(out_11), .out_17(out_12), .out_18(out_13), .out_19(out_14),
    .out_20(out_15), .out_21(out_16), .out_22(out_17), .out_23(out_18), .out_24(out_19), .out_25(out_20),
    .out_26(out_21), .out_27(out_22), .out_28(out_23), .out_29(out_24), .out_30(out_25), .out_31(out_26),
    .out_32(out_27), .out_33(out_28), .out_34(out_29), .out_35(out_30), .out_36(out_31), .out_37(out_32),
    .out_38(out_33), .out_39(out_34), .out_40(out_35), .out_41(out_36));
  LED led_43 (.in(I_Type_jalr_t));
  LED led_44 (.in(jalr));
  LED led_45 (.in(I_Type_Load));
  LED led_46 (.in(I_Type_imm));
  \Filtre_Opération_Type_I  \filtre_opération_type_i_1  (
    .lb(lb), .lw(lw), .lh(lh), .addi(addi), .srli(srli), .slli(slli), .ori(ori), .slti(slti), .xori(xori),
    .jalr(jalr), .Fonction_3bit(funct3), .Fonction_7bit(funct7), .I_Type_Load(I_Type_Load),
    .I_Type_imm(I_Type_imm), .I_Type_jalr(I_Type_Jalr), .andi(andi), .I_Type(I_Type));
  Selecteur_UAL selecteur_ual_1 (
    .\Selecteur_opération_UAL (UAL_select), .add(add), .mul(mul), .sub(sub), .sll(sll), .mulh(mulh),
    .slt(slt), .\xor (\xor ), .div(div), .srl(srl), .\or (\or ), .rem(rem), .\and (\and ));
  or or_1 (writeEn, R_Type, I_Type, U_Type, J_Type);
  Register #(.width(32)) register_1 (.D(PC_4), .Q(PC), .clk(in_1));  // open: en, clr
  // Probe on A
  // Probe on UAL_select
  Selecteur_imm selecteur_imm_1 (
    .in_1(imm_I_extend), .in_3(imm_S_extend), .in_5(imm_B_extend), .in_7(imm_U_extend), .in_9(imm_J_extend),
    .imm(imm), .B_sel(B_sel), .I_Type(I_Type), .U_Type(S_Type), .B_Type(B_Type), .S_Type(U_Type),
    .J_Type(J_Type));
  // Probe on imm
  LED led_47 (.in(B_sel));
  \Extendeur_d_Immédiat  \extendeur_d_immédiat_1  (
    .imm_11_0(imm_11_0), .imm_4_0(imm_4_0), .imm_11_5(imm_11_5), .imm_4_1(imm_4_1), .imm_10_5(imm_10_5),
    .B_imm_11(B_imm_11), .imm_12(imm_12), .imm_31_12(imm_31_12), .imm_10_1(imm_10_1), .imm_20(imm_20),
    .imm_I_Extend(imm_I_extend), .imm_S_Extend(imm_S_extend), .imm_B_Extend(imm_B_extend),
    .imm_U_Extend(imm_U_extend), .imm_J_Extend(imm_J_extend), .J_imm_11(J_imm_11), .imm_19_12(imm_19_12));
  UAL ual_1 (.Resultat(res_alu), .Selecteur_UAL(UAL_select), .Flags(FLAGS), .A(A), .B(multiplexer_1_out));
  // Probe on res_alu
  Multiplexer #(.width(32)) multiplexer_1 (.in0(B), .in1(imm), .out(multiplexer_1_out), .sel(B_sel));  // open: en
  // Probe on multiplexer_1_out
  // Probe on FLAGS
  // Probe on imm_J_extend
  // Probe on imm_U_extend
  // Probe on imm_B_extend
  // Probe on imm_S_extend
  // Probe on imm_I_extend

  // Other names for the same wires on the sheet: clk = in_1; r0[31:0] = out_3; r1[31:0] = out_4; r2[31:0] = out_5;
  //   r3[31:0] = out_6; r4[31:0] = out_9; r5[31:0] = out_10; r6[31:0] = out_11; r7[31:0] = out_12; r8[31:0] = out_13;
  //   r9[31:0] = out_14; r10[31:0] = out_15; r11[31:0] = out_16; r12[31:0] = out_17; r13[31:0] = out_18;
  //   r14[31:0] = out_19; r15[31:0] = out_20; r16[31:0] = out_21; r17[31:0] = out_22; r18[31:0] = out_23;
  //   r19[31:0] = out_24; r20[31:0] = out_25; r21[31:0] = out_26; r22[31:0] = out_27; r23[31:0] = out_28;
  //   r24[31:0] = out_29; r25[31:0] = out_30; r26[31:0] = out_31; r27[31:0] = out_32; r28[31:0] = out_33;
  //   r29[31:0] = out_34; r30[31:0] = out_35; r31[31:0] = out_36

  // Notes on the sheet:
  //   utiliser les flag
  //   implémenter d'autre type d'instruction
endmodule

module \Décodeur_Instruction  (
  input  [31:0] Instruction,
  output [6:0] fonction_7bit,
  output [4:0] registre_source_2,
  output [4:0] registre_source_1,
  output \immédiate__12 ,
  output \immédiate__20 ,
  output [2:0] fonction_3bit,
  output [5:0] \immédiate__10_5 ,
  output [4:0] registre_destination,
  output [6:0] \immédiate__11_5 ,
  output [3:0] \immédiate__4_1 ,
  output [9:0] \immédiate__10_1 ,
  output [19:0] \immédiate__31_12 ,
  output [6:0] code_operation,
  output [11:0] \immédiate__11_0 ,
  output [4:0] \immédiate__4_0 ,
  output \B_immédiate__11 ,
  output \J_immédiate__11 ,
  output [7:0] \immédiate__19_12 
);


  assign \B_immédiate__11  = Instruction[7];
  assign code_operation = Instruction[6:0];
  assign fonction_3bit = Instruction[14:12];
  assign fonction_7bit = Instruction[31:25];
  assign \immédiate__4_0  = Instruction[11:7];
  assign \immédiate__4_1  = Instruction[11:8];
  assign \immédiate__10_1  = Instruction[30:21];
  assign \immédiate__10_5  = Instruction[30:25];
  assign \immédiate__11_0  = Instruction[31:20];
  assign \immédiate__11_5  = Instruction[31:25];
  assign \immédiate__12  = Instruction[31];
  assign \immédiate__19_12  = Instruction[19:12];
  assign \immédiate__20  = Instruction[31];
  assign \immédiate__31_12  = Instruction[31:12];
  assign \J_immédiate__11  = Instruction[20];
  assign registre_destination = Instruction[11:7];
  assign registre_source_1 = Instruction[19:15];
  assign registre_source_2 = Instruction[24:20];

  // Notes on the sheet:
  //   R-Type
  //   I-Type
  //   S-Type
  //   B-Type
  //   U-Type
  //   J-Type
endmodule

module Filtre_Type (
  input  [6:0] code_operation,
  output R_Type,
  output I_Type_Charge,
  output I_Type_Immediat,
  output I_Type_Jalr,
  output S_Type,
  output B_Type,
  output U_Type,
  output J_Type
);

  Comparator #(.width(7)) comparator_1 (.a(code_operation), .b(7'b0110011), .eq(R_Type));  // open: gt, lt
  Comparator #(.width(7)) comparator_2 (.a(code_operation), .b(7'b0000011), .eq(I_Type_Charge));  // open: gt, lt
  Comparator #(.width(7)) comparator_3 (.a(code_operation), .b(7'b0010011), .eq(I_Type_Immediat));  // open: gt, lt
  Comparator #(.width(7)) comparator_4 (.a(code_operation), .b(7'b1100111), .eq(I_Type_Jalr));  // open: gt, lt
  Comparator #(.width(7)) comparator_5 (.a(code_operation), .b(7'b0100011), .eq(S_Type));  // open: gt, lt
  Comparator #(.width(7)) comparator_6 (.a(code_operation), .b(7'b1100011), .eq(B_Type));  // open: gt, lt
  Comparator #(.width(7)) comparator_7 (.a(code_operation), .b(7'b0110111), .eq(U_Type));  // open: gt, lt
  Comparator #(.width(7)) comparator_8 (.a(code_operation), .b(7'b1101111), .eq(J_Type));  // open: gt, lt
endmodule

module \Filtre_Opération_Type_R  (
  input  [2:0] Fonction_3bit,
  input  [6:0] Fonction_7bit,
  input  R_Type,
  output add,
  output \xor ,
  output mul,
  output div,
  output sub,
  output srl,
  output sll,
  output \or ,
  output mulh,
  output rem,
  output slt,
  output \and 
);

  wire and_1_out, and_2_out, and_3_out, and_4_out, and_5_out, and_6_out, and_13_out, and_14_out, and_15_out,
       and_16_out, and_17_out, and_18_out, comparator_1_eq, comparator_2_eq, comparator_3_eq,
       comparator_4_eq, comparator_5_eq, comparator_6_eq, comparator_7_eq, comparator_8_eq, comparator_9_eq,
       comparator_10_eq, comparator_11_eq, comparator_12_eq, comparator_13_eq, comparator_14_eq,
       comparator_15_eq, comparator_16_eq, comparator_17_eq, comparator_18_eq, comparator_19_eq,
       comparator_20_eq, comparator_21_eq, comparator_22_eq, comparator_23_eq, comparator_24_eq;

  Comparator #(.width(3)) comparator_1 (.a(Fonction_3bit), .b(3'b000), .eq(comparator_1_eq));  // open: gt, lt
  Comparator #(.width(7)) comparator_2 (.a(Fonction_7bit), .b({7{1'b0}}), .eq(comparator_2_eq));  // open: gt, lt
  Comparator #(.width(3)) comparator_3 (.a(Fonction_3bit), .b(3'b000), .eq(comparator_3_eq));  // open: gt, lt
  Comparator #(.width(7)) comparator_4 (.a(Fonction_7bit), .b(7'b0000001), .eq(comparator_4_eq));  // open: gt, lt
  Comparator #(.width(3)) comparator_5 (.a(Fonction_3bit), .b(3'b000), .eq(comparator_5_eq));  // open: gt, lt
  Comparator #(.width(7)) comparator_6 (.a(Fonction_7bit), .b(7'b0100000), .eq(comparator_6_eq));  // open: gt, lt
  Comparator #(.width(3)) comparator_7 (.a(Fonction_3bit), .b(3'b001), .eq(comparator_7_eq));  // open: gt, lt
  Comparator #(.width(7)) comparator_8 (.a(Fonction_7bit), .b({7{1'b0}}), .eq(comparator_8_eq));  // open: gt, lt
  Comparator #(.width(3)) comparator_9 (.a(Fonction_3bit), .b(3'b001), .eq(comparator_9_eq));  // open: gt, lt
  Comparator #(.width(7)) comparator_10 (.a(Fonction_7bit), .b(7'b0000001), .eq(comparator_10_eq));  // open: gt, lt
  Comparator #(.width(3)) comparator_11 (.a(Fonction_3bit), .b(3'b010), .eq(comparator_11_eq));  // open: gt, lt
  Comparator #(.width(7)) comparator_12 (.a(Fonction_7bit), .b({7{1'b0}}), .eq(comparator_12_eq));  // open: gt, lt
  and and_1 (and_1_out, comparator_1_eq, comparator_2_eq);
  and and_2 (and_2_out, comparator_3_eq, comparator_4_eq);
  and and_3 (and_3_out, comparator_5_eq, comparator_6_eq);
  and and_4 (and_4_out, comparator_7_eq, comparator_8_eq);
  and and_5 (and_5_out, comparator_9_eq, comparator_10_eq);
  and and_6 (and_6_out, comparator_11_eq, comparator_12_eq);
  and and_7 (add, R_Type, and_1_out);
  and and_8 (mul, R_Type, and_2_out);
  and and_9 (sub, R_Type, and_3_out);
  and and_10 (sll, R_Type, and_4_out);
  and and_11 (mulh, R_Type, and_5_out);
  and and_12 (slt, R_Type, and_6_out);
  Comparator #(.width(3)) comparator_13 (.a(Fonction_3bit), .b(3'b100), .eq(comparator_13_eq));  // open: gt, lt
  Comparator #(.width(7)) comparator_14 (.a(Fonction_7bit), .b({7{1'b0}}), .eq(comparator_14_eq));  // open: gt, lt
  Comparator #(.width(3)) comparator_15 (.a(Fonction_3bit), .b(3'b100), .eq(comparator_15_eq));  // open: gt, lt
  Comparator #(.width(7)) comparator_16 (.a(Fonction_7bit), .b(7'b0000001), .eq(comparator_16_eq));  // open: gt, lt
  Comparator #(.width(3)) comparator_17 (.a(Fonction_3bit), .b(3'b101), .eq(comparator_17_eq));  // open: gt, lt
  Comparator #(.width(7)) comparator_18 (.a(Fonction_7bit), .b({7{1'b0}}), .eq(comparator_18_eq));  // open: gt, lt
  Comparator #(.width(3)) comparator_19 (.a(Fonction_3bit), .b(3'b110), .eq(comparator_19_eq));  // open: gt, lt
  Comparator #(.width(7)) comparator_20 (.a(Fonction_7bit), .b({7{1'b0}}), .eq(comparator_20_eq));  // open: gt, lt
  Comparator #(.width(3)) comparator_21 (.a(Fonction_3bit), .b(3'b110), .eq(comparator_21_eq));  // open: gt, lt
  Comparator #(.width(7)) comparator_22 (.a(Fonction_7bit), .b(7'b0000001), .eq(comparator_22_eq));  // open: gt, lt
  Comparator #(.width(3)) comparator_23 (.a(Fonction_3bit), .b(3'b111), .eq(comparator_23_eq));  // open: gt, lt
  Comparator #(.width(7)) comparator_24 (.a(Fonction_7bit), .b({7{1'b0}}), .eq(comparator_24_eq));  // open: gt, lt
  and and_13 (and_13_out, comparator_13_eq, comparator_14_eq);
  and and_14 (and_14_out, comparator_15_eq, comparator_16_eq);
  and and_15 (and_15_out, comparator_17_eq, comparator_18_eq);
  and and_16 (and_16_out, comparator_19_eq, comparator_20_eq);
  and and_17 (and_17_out, comparator_21_eq, comparator_22_eq);
  and and_18 (and_18_out, comparator_23_eq, comparator_24_eq);
  and and_19 (\xor , R_Type, and_13_out);
  and and_20 (div, R_Type, and_14_out);
  and and_21 (srl, R_Type, and_15_out);
  and and_22 (\or , R_Type, and_16_out);
  and and_23 (rem, R_Type, and_17_out);
  and and_24 (\and , R_Type, and_18_out);

  // Notes on the sheet:
  //   Addition
  //   Multiplication
  //   Soustraction
  //   Comparaison signé
  //   Décalage_gauche
  //   Demi_Multiplication
  //   XOR Logiqe
  //   Division
  //   Decalage_Droite
  //   OU Logique
  //   Modulo
  //   ET Logique
endmodule

module \Filtre_Opération_Type_I  (
  input  [2:0] Fonction_3bit,
  input  [6:0] Fonction_7bit,
  input  I_Type_Load,
  input  I_Type_imm,
  input  I_Type_jalr,
  output lb,
  output lw,
  output lh,
  output I_Type,
  output addi,
  output srli,
  output slli,
  output ori,
  output slti,
  output andi,
  output xori,
  output jalr
);

  wire and_4_out, and_10_out, comparator_1_eq, comparator_2_eq, comparator_3_eq, comparator_4_eq,
       comparator_5_eq, comparator_6_eq, comparator_7_eq, comparator_8_eq, comparator_9_eq, comparator_10_eq,
       comparator_11_eq, comparator_12_eq, comparator_13_eq;

  Comparator #(.width(3)) comparator_1 (.a(Fonction_3bit), .b(3'b000), .eq(comparator_1_eq));  // open: gt, lt
  Comparator #(.width(3)) comparator_2 (.a(Fonction_3bit), .b(3'b001), .eq(comparator_2_eq));  // open: gt, lt
  Comparator #(.width(3)) comparator_3 (.a(Fonction_3bit), .b(3'b000), .eq(comparator_3_eq));  // open: gt, lt
  Comparator #(.width(3)) comparator_4 (.a(Fonction_3bit), .b(3'b001), .eq(comparator_4_eq));  // open: gt, lt
  Comparator #(.width(7)) comparator_5 (.a(Fonction_7bit), .b({7{1'b0}}), .eq(comparator_5_eq));  // open: gt, lt
  Comparator #(.width(3)) comparator_6 (.a(Fonction_3bit), .b(3'b010), .eq(comparator_6_eq));  // open: gt, lt
  Comparator #(.width(3)) comparator_7 (.a(Fonction_3bit), .b(3'b100), .eq(comparator_7_eq));  // open: gt, lt
  Comparator #(.width(3)) comparator_8 (.a(Fonction_3bit), .b(3'b000), .eq(comparator_8_eq));  // open: gt, lt
  and and_1 (lb, I_Type_Load, comparator_1_eq);
  and and_2 (lh, I_Type_Load, comparator_2_eq);
  and and_3 (addi, I_Type_imm, comparator_3_eq);
  and and_4 (and_4_out, comparator_4_eq, comparator_5_eq);
  and and_5 (slti, I_Type_imm, comparator_6_eq);
  and and_6 (xori, I_Type_imm, comparator_7_eq);
  and and_7 (jalr, I_Type_jalr, comparator_8_eq);
  and and_8 (slli, I_Type_imm, and_4_out);
  and and_9 (lw, I_Type_Load, comparator_9_eq);
  Comparator #(.width(3)) comparator_9 (.a(Fonction_3bit), .b(3'b010), .eq(comparator_9_eq));  // open: gt, lt
  Comparator #(.width(3)) comparator_10 (.a(Fonction_3bit), .b(3'b101), .eq(comparator_10_eq));  // open: gt, lt
  Comparator #(.width(7)) comparator_11 (.a(Fonction_7bit), .b({7{1'b0}}), .eq(comparator_11_eq));  // open: gt, lt
  and and_10 (and_10_out, comparator_10_eq, comparator_11_eq);
  Comparator #(.width(3)) comparator_12 (.a(Fonction_3bit), .b(3'b110), .eq(comparator_12_eq));  // open: gt, lt
  Comparator #(.width(3)) comparator_13 (.a(Fonction_3bit), .b(3'b111), .eq(comparator_13_eq));  // open: gt, lt
  and and_11 (srli, I_Type_imm, and_10_out);
  and and_12 (ori, I_Type_imm, comparator_12_eq);
  and and_13 (andi, I_Type_imm, comparator_13_eq);
  or or_1 (I_Type, I_Type_Load, I_Type_imm, I_Type_jalr);

  // Notes on the sheet:
  //   à Completer
  //   à Completer
  //   à Completer
  //   XOR Logique immdiat
  //   à Completer
  //   Addition immédiate
  //   Décallage a gauche immédiat
  //   à Completer
  //   Ou Logique immédiat
  //   ET Logique immédiat
  //   Décallage a droite immédiat
endmodule

module \Filtre_Opération_Type_S_B_U_J  (
  input  [2:0] Fonction_3bit,
  input  S_Type,
  input  B_Type,
  input  U_Type,
  input  J_Type,
  output sw,
  output swge,
  output beq,
  output blt,
  output bltu,
  output lui,
  output jal
);

  wire comparator_1_eq, comparator_2_eq, comparator_3_eq, comparator_4_eq, comparator_5_eq;

  Comparator #(.width(3)) comparator_1 (.a(Fonction_3bit), .b(3'b010), .eq(comparator_1_eq));  // open: gt, lt
  Comparator #(.width(3)) comparator_2 (.a(Fonction_3bit), .b(3'b000), .eq(comparator_2_eq));  // open: gt, lt
  Comparator #(.width(3)) comparator_3 (.a(Fonction_3bit), .b(3'b110), .eq(comparator_3_eq));  // open: gt, lt
  and and_1 (sw, S_Type, comparator_1_eq);
  and and_2 (beq, B_Type, comparator_2_eq);
  and and_3 (bltu, B_Type, comparator_3_eq);
  Comparator #(.width(3)) comparator_4 (.a(Fonction_3bit), .b(3'b111), .eq(comparator_4_eq));  // open: gt, lt
  Comparator #(.width(3)) comparator_5 (.a(Fonction_3bit), .b(3'b100), .eq(comparator_5_eq));  // open: gt, lt
  and and_4 (swge, S_Type, comparator_4_eq);
  and and_5 (blt, B_Type, comparator_5_eq);

  assign jal = J_Type;
  assign lui = U_Type;

  // Notes on the sheet:
  //   à Completer
  //   à Completer
  //   à Completer
  //   à Completer
  //   à Completer
endmodule

module UAL (
  input  [31:0] A,
  input  [31:0] B,
  input  [3:0] Selecteur_UAL,
  output [31:0] Resultat,
  output [3:0] Flags
);

  wire comparator_1_lt;
  wire [31:0] op_add, op_and, op_div, op_mul, op_mulh, op_or, op_rem, op_sll, op_slt, op_srl, op_sub, op_xor,
       shifter_3_out;

  Multiplexer #(.select(4), .width(32)) multiplexer_1 (
    .in0(op_add), .in1(op_mul), .in2(op_sub), .in3(op_sll), .in4(op_mulh), .in5(op_slt), .in6(op_xor),
    .in7(op_div), .in8(op_srl), .in9(op_or), .in10(op_rem), .in11(op_and), .out(Resultat), .sel(Selecteur_UAL));  // open: in12, in13, in14, in15, en
  Adder #(.width(32)) adder_1 (.a(A), .b(B), .out(op_add), .cout(Flags[1]));  // open: cin
  Multiplier #(.width(32)) multiplier_1 (.a(A), .b(B), .out(op_mul));  // open: cin, cout
  Subtractor #(.width(32)) subtractor_1 (.a(A), .b(B), .out(op_sub));  // open: bin, bout
  Shifter #(.width(32)) shifter_1 (.in(A), .\dist (B[4:0]), .out(op_sll));
  Multiplier #(.width(32)) multiplier_2 (.a(A), .b(B), .cout(op_mulh));  // open: out, cin
  Comparator #(.width(32)) comparator_1 (.a(A), .b(B), .lt(comparator_1_lt));  // open: gt, eq
  assign op_xor = A ^ B;  // XOR_Gate xor_1, 32 bits wide
  assign op_slt = {{31{1'b0}}, comparator_1_lt};  // Bit_Extender bit_extender_1
  Divider #(.width(32)) divider_1 (.a(A), .b(B), .out(op_div));  // open: upper, rem
  Shifter #(.width(32), .shift("lr")) shifter_2 (.in(A), .\dist (B[4:0]), .out(op_srl));
  assign op_or = A | B;  // OR_Gate or_1, 32 bits wide
  Divider #(.width(32)) divider_2 (.a(A), .b(B), .rem(op_rem));  // open: out, upper
  assign op_and = A & B;  // AND_Gate and_1, 32 bits wide
  Shifter #(.width(32), .shift("lr")) shifter_3 (.in(A), .\dist (B[4:0]), .out(shifter_3_out));
  Comparator #(.width(32)) comparator_2 (.a(A), .b(B), .eq(Flags[0]));  // open: gt, lt

  assign Flags[3:2] = 2'b00;

  // Other names for the same wires on the sheet: Equal = Flags[0]; cout = Flags[1]
endmodule

module Selecteur_UAL (
  input  add,
  input  mul,
  input  sub,
  input  sll,
  input  mulh,
  input  slt,
  input  \xor ,
  input  div,
  input  srl,
  input  \or ,
  input  rem,
  input  \and ,
  output [3:0] \Selecteur_opération_UAL 
);

  wire [3:0] adder_1_out, adder_2_out, adder_3_out, adder_4_out, adder_5_out, adder_6_out, adder_7_out,
       adder_8_out, adder_9_out, adder_10_out, adder_11_out, adder_12_out, multiplexer_1_out,
       multiplexer_2_out, multiplexer_3_out, multiplexer_4_out, multiplexer_5_out, multiplexer_6_out,
       multiplexer_7_out, multiplexer_8_out, multiplexer_9_out, multiplexer_10_out, multiplexer_11_out,
       multiplexer_12_out;

  Multiplexer #(.width(4)) multiplexer_1 (
    .in0(4'b0000), .in1(4'b0000), .out(multiplexer_1_out), .sel(add));  // open: en
  Multiplexer #(.width(4)) multiplexer_2 (
    .in0(4'b0000), .in1(4'b0001), .out(multiplexer_2_out), .sel(mul));  // open: en
  Multiplexer #(.width(4)) multiplexer_3 (
    .in0(4'b0000), .in1(4'b0010), .out(multiplexer_3_out), .sel(sub));  // open: en
  Multiplexer #(.width(4)) multiplexer_4 (
    .in0(4'b0000), .in1(4'b0011), .out(multiplexer_4_out), .sel(sll));  // open: en
  Multiplexer #(.width(4)) multiplexer_5 (
    .in0(4'b0000), .in1(4'b0100), .out(multiplexer_5_out), .sel(mulh));  // open: en
  Multiplexer #(.width(4)) multiplexer_6 (
    .in0(4'b0000), .in1(4'b0101), .out(multiplexer_6_out), .sel(slt));  // open: en
  Multiplexer #(.width(4)) multiplexer_7 (
    .in0(4'b0000), .in1(4'b0110), .out(multiplexer_7_out), .sel(\xor ));  // open: en
  Multiplexer #(.width(4)) multiplexer_8 (
    .in0(4'b0000), .in1(4'b0111), .out(multiplexer_8_out), .sel(div));  // open: en
  Multiplexer #(.width(4)) multiplexer_9 (
    .in0(4'b0000), .in1(4'b1000), .out(multiplexer_9_out), .sel(srl));  // open: en
  Multiplexer #(.width(4)) multiplexer_10 (
    .in0(4'b0000), .in1(4'b1001), .out(multiplexer_10_out), .sel(\or ));  // open: en
  Multiplexer #(.width(4)) multiplexer_11 (
    .in0(4'b0000), .in1(4'b1010), .out(multiplexer_11_out), .sel(rem));  // open: en
  Multiplexer #(.width(4)) multiplexer_12 (
    .in0(4'b0000), .in1(4'b1011), .out(multiplexer_12_out), .sel(\and ));  // open: en
  Adder #(.width(4)) adder_1 (.a(multiplexer_1_out), .b(multiplexer_2_out), .out(adder_1_out));  // open: cin, cout
  Adder #(.width(4)) adder_2 (.a(multiplexer_3_out), .b(multiplexer_4_out), .out(adder_2_out));  // open: cin, cout
  Adder #(.width(4)) adder_3 (.a(multiplexer_5_out), .b(multiplexer_6_out), .out(adder_3_out));  // open: cin, cout
  Adder #(.width(4)) adder_4 (.a(multiplexer_7_out), .b(multiplexer_8_out), .out(adder_4_out));  // open: cin, cout
  Adder #(.width(4)) adder_5 (.a(multiplexer_9_out), .b(multiplexer_10_out), .out(adder_5_out));  // open: cin, cout
  Adder #(.width(4)) adder_6 (.a(multiplexer_11_out), .b(multiplexer_12_out), .out(adder_6_out));  // open: cin, cout
  Adder #(.width(4)) adder_7 (.a(adder_1_out), .b(adder_2_out), .out(adder_7_out));  // open: cin, cout
  Adder #(.width(4)) adder_8 (.a(adder_3_out), .b(adder_4_out), .out(adder_8_out));  // open: cin, cout
  Adder #(.width(4)) adder_9 (.a(adder_5_out), .b(adder_6_out), .out(adder_9_out));  // open: cin, cout
  Adder #(.width(4)) adder_10 (.a(4'b0000), .b(4'b0000), .out(adder_10_out));  // open: cin, cout
  Adder #(.width(4)) adder_11 (.a(adder_7_out), .b(adder_8_out), .out(adder_11_out));  // open: cin, cout
  Adder #(.width(4)) adder_12 (.a(adder_9_out), .b(adder_10_out), .out(adder_12_out));  // open: cin, cout
  Adder #(.width(4)) adder_13 (.a(adder_11_out), .b(adder_12_out), .out(\Selecteur_opération_UAL ));  // open: cin, cout
endmodule

module Compteur_De_Programme (
  input  [31:0] PC,
  output [31:0] PC_4,
  output [31:0] fetch_addr
);

  Adder #(.width(32)) adder_1 (.a(PC), .b(32'h4), .out(PC_4));  // open: cin, cout
  Shifter #(.width(32), .shift("lr")) shifter_1 (.in(PC), .\dist (5'b00010), .out(fetch_addr));
endmodule

module Banc_De_Registre (
  input  [4:0] adresse,
  input  [4:0] adresse_2,
  input  [4:0] adresse_3,
  input  \écriture ,
  input  horloge,
  input  reset,
  input  [31:0] in_7,
  output [31:0] out_8,
  output [31:0] out_9,
  output [31:0] out_10,
  output [31:0] out_11,
  output [31:0] out_12,
  output [31:0] out_13,
  output [31:0] out_14,
  output [31:0] out_15,
  output [31:0] out_16,
  output [31:0] out_17,
  output [31:0] out_18,
  output [31:0] out_19,
  output [31:0] out_20,
  output [31:0] out_21,
  output [31:0] out_22,
  output [31:0] out_23,
  output [31:0] out_24,
  output [31:0] out_25,
  output [31:0] out_26,
  output [31:0] out_27,
  output [31:0] out_28,
  output [31:0] out_29,
  output [31:0] out_30,
  output [31:0] out_31,
  output [31:0] out_32,
  output [31:0] out_33,
  output [31:0] out_34,
  output [31:0] out_35,
  output [31:0] out_36,
  output [31:0] out_37,
  output [31:0] out_38,
  output [31:0] out_39,
  output [31:0] out_40,
  output [31:0] out_41
);

  wire [31:0] demultiplexer_1_out14, demultiplexer_1_out16, in_r1, in_r2, in_r3, in_r4, in_r5, in_r6, in_r7,
       in_r8, in_r9, in_r10, in_r11, in_r12, in_r13, in_r14, in_r15, in_r16, in_r17, in_r18, in_r19, in_r20,
       in_r21, in_r22, in_r23, in_r24, in_r25, in_r26, in_r27, in_r28, in_r29, in_r30, in_r31;

  Register #(.width(32)) r0 (.en(\écriture ), .Q(out_10), .clk(horloge), .clr(reset));  // open: D
  Register #(.width(32)) r4 (.D(in_r4), .en(\écriture ), .Q(out_14), .clk(horloge), .clr(reset));
  Register #(.width(32)) r8 (.D(in_r8), .en(\écriture ), .Q(out_18), .clk(horloge), .clr(reset));
  Register #(.width(32)) r12 (.D(in_r12), .en(\écriture ), .Q(out_22), .clk(horloge), .clr(reset));
  Register #(.width(32)) r16 (.D(in_r16), .en(\écriture ), .Q(out_26), .clk(horloge), .clr(reset));
  Register #(.width(32)) r20 (.D(in_r20), .en(\écriture ), .Q(out_30), .clk(horloge), .clr(reset));
  Register #(.width(32)) r24 (.D(in_r24), .en(\écriture ), .Q(out_34), .clk(horloge), .clr(reset));
  Register #(.width(32)) r28 (.D(in_r28), .en(\écriture ), .Q(out_38), .clk(horloge), .clr(reset));
  Demultiplexer #(.select(5), .width(32)) demultiplexer_1 (
    .out1(in_r1), .out2(in_r2), .out3(in_r3), .out4(in_r4), .out5(in_r5), .out6(in_r6), .out7(in_r7),
    .out8(in_r8), .out9(in_r9), .out10(in_r10), .out11(in_r11), .out12(in_r12), .out13(in_r13),
    .out14(demultiplexer_1_out14), .out15(in_r15), .out16(demultiplexer_1_out16), .out17(in_r17),
    .out18(in_r18), .out19(in_r19), .out20(in_r20), .out21(in_r21), .out22(in_r22), .out23(in_r23),
    .out24(in_r24), .out25(in_r25), .out26(in_r26), .out27(in_r27), .out28(in_r28), .out29(in_r29),
    .out30(in_r30), .out31(in_r31), .in(in_7), .sel(adresse_3));  // open: out0, en
  Register #(.width(32)) r1 (.D(in_r1), .en(\écriture ), .Q(out_11), .clk(horloge), .clr(reset));
  Register #(.width(32)) r5 (.D(in_r5), .en(\écriture ), .Q(out_15), .clk(horloge), .clr(reset));
  Register #(.width(32)) r9 (.D(in_r9), .en(\écriture ), .Q(out_19), .clk(horloge), .clr(reset));
  Register #(.width(32)) r13 (.D(in_r13), .en(\écriture ), .Q(out_23), .clk(horloge), .clr(reset));
  Register #(.width(32)) r17 (.D(in_r17), .en(\écriture ), .Q(out_27), .clk(horloge), .clr(reset));
  Register #(.width(32)) r21 (.D(in_r21), .en(\écriture ), .Q(out_31), .clk(horloge), .clr(reset));
  Register #(.width(32)) r25 (.D(in_r25), .en(\écriture ), .Q(out_35), .clk(horloge), .clr(reset));
  Register #(.width(32)) r29 (.D(in_r29), .en(\écriture ), .Q(out_39), .clk(horloge), .clr(reset));
  Register #(.width(32)) r2 (.D(in_r2), .en(\écriture ), .Q(out_12), .clk(horloge), .clr(reset));
  Register #(.width(32)) r6 (.D(in_r6), .en(\écriture ), .Q(out_16), .clk(horloge), .clr(reset));
  Register #(.width(32)) r10 (.D(in_r10), .en(\écriture ), .Q(out_20), .clk(horloge), .clr(reset));
  Register #(.width(32)) r14 (.D(in_r14), .en(\écriture ), .Q(out_24), .clk(horloge), .clr(reset));
  Register #(.width(32)) r18 (.D(in_r18), .en(\écriture ), .Q(out_28), .clk(horloge), .clr(reset));
  Register #(.width(32)) r22 (.D(in_r22), .en(\écriture ), .Q(out_32), .clk(horloge), .clr(reset));
  Register #(.width(32)) r26 (.D(in_r26), .en(\écriture ), .Q(out_36), .clk(horloge), .clr(reset));
  Register #(.width(32)) r30 (.D(in_r30), .en(\écriture ), .Q(out_40), .clk(horloge), .clr(reset));
  Register #(.width(32)) r3 (.D(in_r3), .en(\écriture ), .Q(out_13), .clk(horloge), .clr(reset));
  Register #(.width(32)) r7 (.D(in_r7), .en(\écriture ), .Q(out_17), .clk(horloge), .clr(reset));
  Register #(.width(32)) r11 (.D(in_r11), .en(\écriture ), .Q(out_21), .clk(horloge), .clr(reset));
  Register #(.width(32)) r15 (.D(in_r15), .en(\écriture ), .Q(out_25), .clk(horloge), .clr(reset));
  Register #(.width(32)) r19 (.D(in_r19), .en(\écriture ), .Q(out_29), .clk(horloge), .clr(reset));
  Register #(.width(32)) r23 (.D(in_r23), .en(\écriture ), .Q(out_33), .clk(horloge), .clr(reset));
  Register #(.width(32)) r27 (.D(in_r27), .en(\écriture ), .Q(out_37), .clk(horloge), .clr(reset));
  Register #(.width(32)) r31 (.D(in_r31), .en(\écriture ), .Q(out_41), .clk(horloge), .clr(reset));
  Multiplexer #(.select(5), .width(32)) multiplexer_1 (
    .in0(out_10), .in1(out_11), .in2(out_12), .in3(out_13), .in4(out_14), .in5(out_15), .in6(out_16),
    .in7(out_17), .in8(out_18), .in9(out_19), .in10(out_20), .in11(out_21), .in12(out_22), .in13(out_23),
    .in14(out_24), .in15(out_25), .in16(out_26), .in17(out_27), .in18(out_28), .in19(out_29), .in20(out_30),
    .in21(out_31), .in22(out_32), .in23(out_33), .in24(out_34), .in25(out_35), .in26(out_36), .in27(out_37),
    .in28(out_38), .in29(out_39), .in30(out_40), .in31(out_41), .out(out_8), .sel(adresse));  // open: en
  Multiplexer #(.select(5), .width(32)) multiplexer_2 (
    .in0(out_10), .in1(out_11), .in2(out_12), .in3(out_13), .in4(out_14), .in5(out_15), .in6(out_16),
    .in7(out_17), .in8(out_18), .in9(out_19), .in10(out_20), .in11(out_21), .in12(out_22), .in13(out_23),
    .in14(out_24), .in15(out_25), .in16(out_26), .in17(out_27), .in18(out_28), .in19(out_29), .in20(out_30),
    .in21(out_31), .in22(out_32), .in23(out_33), .in24(out_34), .in25(out_35), .in26(out_36), .in27(out_37),
    .in28(out_38), .in29(out_39), .in30(out_40), .in31(out_41), .out(out_9), .sel(adresse_2));  // open: en

  // Other names for the same wires on the sheet: A[31:0] = out_8; B[31:0] = out_9; clk = horloge; data[31:0] = in_7;
  //   out_r0[31:0] = out_10; out_r1[31:0] = out_11; out_r2[31:0] = out_12; out_r3[31:0] = out_13;
  //   out_r4[31:0] = out_14; out_r5[31:0] = out_15; out_r6[31:0] = out_16; out_r7[31:0] = out_17;
  //   out_r8[31:0] = out_18; out_r9[31:0] = out_19; out_r10[31:0] = out_20; out_r11[31:0] = out_21;
  //   out_r12[31:0] = out_22; out_r13[31:0] = out_23; out_r14[31:0] = out_24; out_r15[31:0] = out_25;
  //   out_r16[31:0] = out_26; out_r17[31:0] = out_27; out_r18[31:0] = out_28; out_r19[31:0] = out_29;
  //   out_r20[31:0] = out_30; out_r21[31:0] = out_31; out_r22[31:0] = out_32; out_r23[31:0] = out_33;
  //   out_r24[31:0] = out_34; out_r25[31:0] = out_35; out_r26[31:0] = out_36; out_r27[31:0] = out_37;
  //   out_r28[31:0] = out_38; out_r29[31:0] = out_39; out_r30[31:0] = out_40; out_r31[31:0] = out_41;
  //   rd[4:0] = adresse_3; rs1[4:0] = adresse; rs2[4:0] = adresse_2; writeEn = \écriture 
endmodule

module \Extendeur_d_Immédiat  (
  input  [11:0] imm_11_0,
  input  [4:0] imm_4_0,
  input  [6:0] imm_11_5,
  input  [3:0] imm_4_1,
  input  [5:0] imm_10_5,
  input  B_imm_11,
  input  imm_12,
  input  [19:0] imm_31_12,
  input  [9:0] imm_10_1,
  input  J_imm_11,
  input  [7:0] imm_19_12,
  input  imm_20,
  output [31:0] imm_I_Extend,
  output [31:0] imm_S_Extend,
  output [31:0] imm_B_Extend,
  output [31:0] imm_U_Extend,
  output [31:0] imm_J_Extend
);

  assign imm_I_Extend = {{20{1'b0}}, imm_11_0};  // Bit_Extender bit_extender_1
  assign imm_S_Extend = {{20{1'b0}}, {imm_11_5, imm_4_0}};  // Bit_Extender bit_extender_2
  assign imm_B_Extend = {{19{1'b0}}, {imm_12, B_imm_11, imm_10_5, imm_4_1, 1'b0}};  // Bit_Extender bit_extender_3
  assign imm_J_Extend = {{11{1'b0}}, {imm_20, imm_19_12, J_imm_11, imm_10_1, 1'b0}};  // Bit_Extender bit_extender_4

  assign imm_U_Extend = {imm_31_12, {12{1'b0}}};
endmodule

module Selecteur_imm (
  input  [31:0] in_1,
  input  I_Type,
  input  [31:0] in_3,
  input  U_Type,
  input  [31:0] in_5,
  input  B_Type,
  input  [31:0] in_7,
  input  S_Type,
  input  [31:0] in_9,
  input  J_Type,
  output [31:0] imm,
  output B_sel
);

  wire [31:0] adder_1_out, adder_2_out, adder_3_out, multiplexer_1_out, multiplexer_2_out, multiplexer_3_out,
       multiplexer_4_out, multiplexer_5_out;

  Multiplexer #(.width(32)) multiplexer_1 (
    .in0({32{1'b0}}), .in1(in_1), .out(multiplexer_1_out), .sel(I_Type));  // open: en
  Multiplexer #(.width(32)) multiplexer_2 (
    .in0({32{1'b0}}), .in1(in_3), .out(multiplexer_2_out), .sel(U_Type));  // open: en
  Multiplexer #(.width(32)) multiplexer_3 (
    .in0({32{1'b0}}), .in1(in_5), .out(multiplexer_3_out), .sel(B_Type));  // open: en
  Multiplexer #(.width(32)) multiplexer_4 (
    .in0({32{1'b0}}), .in1(in_7), .out(multiplexer_4_out), .sel(S_Type));  // open: en
  or or_1 (B_sel, S_Type, B_Type, U_Type, I_Type);
  Adder #(.width(32)) adder_1 (.a(multiplexer_1_out), .b(multiplexer_2_out), .out(adder_1_out));  // open: cin, cout
  Adder #(.width(32)) adder_2 (.a(multiplexer_3_out), .b(multiplexer_4_out), .out(adder_2_out));  // open: cin, cout
  Adder #(.width(32)) adder_3 (.a(adder_1_out), .b(adder_2_out), .out(adder_3_out));  // open: cin, cout
  Multiplexer #(.width(32)) multiplexer_5 (
    .in0({32{1'b0}}), .in1(in_9), .out(multiplexer_5_out), .sel(J_Type));  // open: en
  Adder #(.width(32)) adder_4 (.a(adder_3_out), .b(multiplexer_5_out), .out(imm));  // open: cin, cout
endmodule
